# Fritzing sketch schematic (saved by Fritzing 0.9.3b)
circuit board: 1.93148cm x 4.46044cm
circuit board: 1.93148cm x 4.46044cm
breadboards: 2

parts:
  J2 = male pin header, 2 pins [form="♂ (male)"]
  J4 = male pin header, 2 pins [form="♂ (male)"]
  Part1 = Arduino Nano (Rev3.0)
  J3 = male pin header, 4 pins [form="♂ (male)"]
  J5 = male pin header, 4 pins [form="♂ (male)"]
  J1 = male pin header, 6 pins [form="♂ (male)"]
  S1 = Momentary Switch [package=ksa_sealed_tac_switch]
  J6 = male pin header, 4 pins [form="♂ (male)"]
  S2 = Momentary Switch [package=ksa_sealed_tac_switch]
  S3 = Momentary Switch [package=ksa_sealed_tac_switch]
  J7 = male pin header, 4 pins [form="♂ (male)"]

nets:
  N1: J2.pin1, Part1.3V3
  N2: J2.pin2, J4.pin2, J1.pin2, J7.pin2
  N3: J4.pin1, Part1.GND, J5.pin4, J1.pin1, J7.pin1
  N4: Part1.D2, J1.pin6
  N5: Part1.D3, J1.pin5
  N6: Part1.D4, J1.pin4
  N7: Part1.D5, J5.pin1
  N8: Part1.D6, J5.pin2
  N9: Part1.D7, J5.pin3
  N10: Part1.D8, J3.pin4
  N11: Part1.D9, J3.pin3
  N12: Part1.D10, J3.pin2
  N13: Part1.D11/MOSI, J3.pin1
  N14: Part1.A5, J7.pin3
  N15: Part1.A4, J7.pin4
  N16: Part1.A0, J1.pin3
  N17: S1.1, J6.pin3
  N18: S1.4, J6.pin4, S2.4, S3.3, S3.4
  N19: J6.pin1, S3.1
  N20: J6.pin2, S2.1

notes:
  main board
  switch board
