# Fritzing sketch scematic (saved by Fritzing 0.9.3b)
circuit board: 6.70895cm x 4.56406cm
breadboards: 1

parts:
  Squix1 = OLED 0.96" 128x64 I2C SSD1306
  S1 = Momentary Switch [package=ksa_sealed_tac_switch]
  S2 = Momentary Switch [package=ksa_sealed_tac_switch]
  S3 = Momentary Switch [package=ksa_sealed_tac_switch]
  Part1 = Arduino Nano (Rev3.0)
  J2 = male pin header, 2 pins [form="♂ (male)"]
  J1 = male pin header, 6 pins [form="♂ (male)"]
  J3 = male pin header, 4 pins [form="♂ (male)"]
  J4 = male pin header, 2 pins [form="♂ (male)"]

nets (from the pcb view):
  N1: Squix1.VCC, J1.pin1
  N2: Squix1.GND, J2.pin2, J1.pin2, J4.pin2
  N3: Squix1.SCL, Part1.A5
  N4: Squix1.SCA, Part1.A4
  N5: S1.1, S1.2, S2.1, S2.2, S3.1, S3.2, Part1.GND, J4.pin1
  N6: S1.3, S1.4, Part1.D5
  N7: S2.3, S2.4, Part1.D6
  N8: S3.3, S3.4, Part1.D7
  N9: Part1.D2, J1.pin6
  N10: Part1.D3, J1.pin5
  N11: Part1.D8, J3.pin4
  N12: Part1.D9, J3.pin3
  N13: Part1.D10, J3.pin2
  N14: Part1.D11/MOSI, J3.pin1
  N15: Part1.3V3, J2.pin1
